# Fritzing sketch RGB-circuit (saved by Fritzing 0.9.2b)
breadboards: 1

parts:
  R1 = Resistor [tolerance=±5% resistance=220 package=THT]
  LED1 = RGB LED (com. cathode, rgb) [package="5 mm [THT]"]
  R2 = Resistor [tolerance=±5% resistance=220 package=THT]
  R3 = Resistor [tolerance=±5% resistance=220 package=THT]
  Part1 = Arduino Nano (Rev3.0)

nets:
  N1: R1.Pin_0, Part1.D6
  N2: R1.Pin_1, LED1.red_anode
  N3: LED1.common_cathode, Part1.GND
  N4: LED1.green_anode, R3.Pin_1
  N5: LED1.blue_anode, R2.Pin_1
  N6: R2.Pin_0, Part1.D5
  N7: R3.Pin_0, Part1.D3
