# Fritzing sketch Speaker (saved by Fritzing 0.9.2b)
breadboards: 1

parts:
  Difuzor = Loudspeaker
  Part1 = Arduino Nano (Rev3.0)
  R1 = Resistor [tolerance=±5% resistance=100 package=THT]

nets:
  N1: Difuzor.pin1, R1.Pin_1
  N2: Difuzor.pin2, Part1.GND
  N3: Part1.D8, R1.Pin_0
