# Fritzing sketch Schema (saved by Fritzing 0.9.2b)
breadboards: 1

parts:
  Arduino_Nano = Arduino Nano v2.3
  R1 = Resistor [tolerance=±5% resistance=220 package=THT]
  LED1 = LED - 5mm [color="Red (633nm)" package="5 mm [THT]"]
  R2 = Resistor [tolerance=±5% resistance=220 package=THT]
  LED2 = LED - 5mm [color="Red (633nm)" package="5 mm [THT]"]
  R3 = Resistor [tolerance=±5% resistance=220 package=THT]
  LED3 = LED - 5mm [color="Red (633nm)" package="5 mm [THT]"]
  R4 = Resistor [tolerance=±5% resistance=220 package=THT]
  LED4 = LED - 5mm [color="Red (633nm)" package="5 mm [THT]"]
  R5 = Resistor [tolerance=±5% resistance=220 package=THT]
  LED5 = LED - 5mm [color="Red (633nm)" package="5 mm [THT]"]
  R6 = Resistor [tolerance=±5% resistance=220 package=THT]
  LED6 = LED - 5mm [color="Red (633nm)" package="5 mm [THT]"]
  R7 = Resistor [tolerance=±5% resistance=220 package=THT]
  LED7 = LED - 5mm [color="Red (633nm)" package="5 mm [THT]"]
  R8 = Resistor [tolerance=±5% resistance=220 package=THT]
  LED8 = LED - 5mm [color="Red (633nm)" package="5 mm [THT]"]

nets:
  N1: Arduino_Nano.GND, LED1.cathode, LED2.cathode, LED3.cathode, LED4.cathode, LED5.cathode, LED6.cathode, LED7.cathode, LED8.cathode
  N2: Arduino_Nano.D2, R1.Pin_1
  N3: Arduino_Nano.D3, R2.Pin_1
  N4: Arduino_Nano.D4, R3.Pin_1
  N5: Arduino_Nano.D5, R4.Pin_1
  N6: Arduino_Nano.D6, R5.Pin_0
  N7: Arduino_Nano.D7, R6.Pin_0
  N8: Arduino_Nano.D8, R7.Pin_0
  N9: Arduino_Nano.D9, R8.Pin_0
  N10: R1.Pin_0, LED1.anode
  N11: R2.Pin_0, LED2.anode
  N12: R3.Pin_0, LED3.anode
  N13: R4.Pin_0, LED4.anode
  N14: R5.Pin_1, LED5.anode
  N15: R6.Pin_1, LED6.anode
  N16: R7.Pin_1, LED7.anode
  N17: R8.Pin_1, LED8.anode
