# Fritzing sketch Masinuta (saved by Fritzing 0.9.2b)

parts:
  Part1 = SRF05 Ultrasonic Rangefinder
  M1 = DC Motor
  VCC1 = 4 x AAA Battery Mount
  Nano1 = Arduino Nano v2.3
  U1 = SWITCH_SPDT [package=kps-1290]
  S1 = H-Bridge with L298N
  M2 = DC Motor

nets:
  VCC: Part1.VCC, Nano1.VIN, U1.P, S1.12V
  N1: Part1.Trig, Nano1.D3
  N2: Part1.Echo, Nano1.D2
  GND: Part1.GND, VCC1.-, Nano1.GND, S1.GND
  N3: M1.pin_1, S1.M1-02
  N4: M1.pin_2, S1.M1-01
  N5: VCC1.+, U1.S
  N6: Nano1.D9, S1.IN4
  N7: Nano1.D10, S1.IN3
  N8: Nano1.D11, S1.IN2
  N9: Nano1.D12, S1.IN1
  N10: S1.ENA, S1.ENA-5V
  N11: S1.ENB, S1.ENB-5V
  N12: S1.M2-01, M2.pin_2
  N13: S1.M2-02, M2.pin_1

custom parts:
  H-Bridge with L298N: h-bridge
